# Fritzing sketch BO-Sensor (saved by Fritzing 0.9.3b)
stripboards: 1
breadboards: 1

parts:
  BO-Sensor = Arduino Uno (Rev3)
  BAT1 = BC9VPC [package=bc9vpc]
  DHT11 = DHT11 Humitidy and Temperature Sensor
  R1 = Resistor [tolerance=±5% resistance=1.0k package="2010 [SMD]"]
  Onderdeel1 = Soil Moisture Sensor
  R2 = Photocell (LDR) [package=THT]
  R3 = Resistor [tolerance=±5% resistance=10k package="2010 [SMD]"]
  R4 = Resistor [tolerance=±5% resistance=4.7k package="2010 [SMD]"]
  DS1 = DS2401+ Serial number [part_number=DS2401+]
  BAT2 = BC9VPC [package=bc9vpc]
  JP18 = Header 1 [package=1x01_offset]
  JP19 = Header 1 [package=1x01_offset]
  JP21 = Header 1 [package=1x01_offset]
  R9 = Resistor [tolerance=±5% resistance=10k package="2010 [SMD]"]
  JP22 = Header 1 [package=1x01_offset]
  JP23 = Header 1 [package=1x01_offset]
  JP24 = Header 1 [package=1x01_offset]
  Onderdeel3 = Soil Moisture Sensor
  HWID = Header 1 [package=1x01_offset]
  DS2 = DS2401+ Serial number [part_number=DS2401+]
  R10 = Resistor [tolerance=±5% resistance=4.7k package="2010 [SMD]"]
  DHT11_2 = Header 1 [package=1x01_offset]
  JP25 = Header 1 [package=1x01_offset]
  JP26 = Header 1 [package=1x01_offset]
  JP27 = Header 1 [package=1x01_offset]
  DHT13 = DHT11 Humitidy and Temperature Sensor
  R11 = Resistor [tolerance=±5% resistance=1.0k package="2010 [SMD]"]
  R12 = Photocell (LDR) [package=THT]
  LDR = Header 1 [package=1x01_offset]
  JP28 = Header 1 [package=1x01_offset]
  FS1000_TX1 = FS1000A - 433Mhz RF Transmitter [package=THT]
  SOIL = Header 1 [package=1x01_offset]
  DHT15 = Header 1 [package=1x01_offset]
  DHT16 = Header 1 [package=1x01_offset]
  DHT17 = Header 1 [package=1x01_offset]
  TX = Header 1 [package=1x01_offset]
  Onderdeel4 = NRF24L01+ Breakout Board

nets:
  N1: BO-Sensor.A0, Onderdeel1.SIG
  N2: BO-Sensor.A1, R2.pin_1, R3.Pin_0
  N3: BO-Sensor.D9_PWM, Onderdeel4.CE
  N4: BO-Sensor.D10_PWM/SS, Onderdeel4.CS
  N5: BO-Sensor.D11_PWM/MOSI, Onderdeel4.MOSI
  N6: BO-Sensor.D12/MISO, Onderdeel4.MISO
  N7: BO-Sensor.D13/SCK, Onderdeel4.SCK
  GND: BO-Sensor.GND, BAT1.V-, Onderdeel4.GND
  N8: BO-Sensor.D2, R4.Pin_0, DS1.DQ
  N9: BO-Sensor.D4, DHT11.DATA, R1.Pin_0
  3V3: BO-Sensor.3V3, Onderdeel4.VCC
  N10: BO-Sensor.VIN, BAT1.V+
  VDD: DHT11.VDD, R1.Pin_1, Onderdeel1.VCC, R2.pin_0, R4.Pin_1
  GND_2: DHT11.GND, Onderdeel1.GND, R3.Pin_1, DS1.GND
  VCC: BAT2.V+, JP19.1, JP21.1, JP24.1, Onderdeel3.VCC, R10.Pin_0, JP26.1, DHT13.VDD, R11.Pin_1, R12.pin_0, FS1000_TX1.VCC, DHT15.1
  GND_3: BAT2.V-, JP18.1, R9.Pin_0, JP22.1, Onderdeel3.GND, DS2.GND, JP25.1, DHT13.GND, FS1000_TX1.GND, DHT17.1
  N11: R9.Pin_1, R12.pin_1, LDR.1, JP28.1
  N12: JP23.1, DHT11_2.1, DHT13.DATA, R11.Pin_0
  N13: Onderdeel3.SIG, JP27.1, SOIL.1
  N14: HWID.1, DS2.DQ, R10.Pin_1
  N15: FS1000_TX1.DATA, DHT16.1, TX.1

custom parts:
  DHT11 Humitidy and Temperature Sensor: DHT11 Humidity and Temperature Sensor
  DS2401+ Serial number: 64-bit ROM Silicon Serial Number ICs with unique factory-written 48-bit serial numbers. These devices provide a unique identity that can easily be determined with a minimal electronic interface using a 1-wire protocol.
  FS1000A - 433Mhz RF Transmitter: This is 433Mhz RF transmitter with receiver kit for Arduino ARM MCU wireless Application environment: Remote control switch, receiver module, motorcycles, automobile anti-theft products, home security products, electric doors, shutter doors, windows, remote control socket, remote control LED, remote audio remote control electric doors, garage door remote control, remote control retractable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
