# Fritzing sketch Rambo_Actor (saved by Fritzing 0.9.3b)
breadboards: 1

parts:
  Onderdeel1 = Arduino Uno (Rev3)
  Onderdeel2 = NRF24L01+ Breakout Board
  LED1 = smd LED [color="Blue (505nm)" package="0603 [SMD]"]
  LED2 = smd LED [color="Yellow (595nm)" package="0603 [SMD]"]
  LED3 = smd LED [color="Red (633nm)" package="0603 [SMD]"]
  R1 = Resistor [tolerance=±5% resistance=220 package=THT]
  R2 = Resistor [tolerance=±5% resistance=220 package=THT]
  R3 = Resistor [tolerance=±5% resistance=220 package=THT]
  BAT1 = BC9VPC [package=bc9vpc]

nets:
  N1: Onderdeel1.D9_PWM, Onderdeel2.CE
  N2: Onderdeel1.D10_PWM/SS, Onderdeel2.CS
  N3: Onderdeel1.D11_PWM/MOSI, Onderdeel2.MOSI
  N4: Onderdeel1.D12/MISO, Onderdeel2.MISO
  N5: Onderdeel1.D13/SCK, Onderdeel2.SCK
  GND: Onderdeel1.GND, Onderdeel2.GND, LED1.cathode, LED2.cathode, LED3.cathode, BAT1.V-
  N6: Onderdeel1.D5_PWM, R3.Pin_0
  N7: Onderdeel1.D6_PWM, R2.Pin_0
  N8: Onderdeel1.D7, R1.Pin_0
  3V3: Onderdeel1.3V3, Onderdeel2.VCC
  N9: Onderdeel1.VIN, BAT1.V+
  N10: LED1.anode, R1.Pin_1
  N11: LED2.anode, R2.Pin_1
  N12: LED3.anode, R3.Pin_1
