# Fritzing sketch Rambo_Node (saved by Fritzing 0.9.3b)

parts:
  Raspberry_Pi_1 = Raspberry Pi 3 [part_number=RPI-3-V1.2]
  Onderdeel1 = NRF24L01+ Breakout Board

nets:
  3V3: Raspberry_Pi_1.3v3, Onderdeel1.VCC
  GND: Raspberry_Pi_1.GND, Onderdeel1.GND
  N1: Raspberry_Pi_1.GPIO17, Onderdeel1.CS
  N2: Raspberry_Pi_1.GPIO10, Onderdeel1.SCK
  N3: Raspberry_Pi_1.GPIO9, Onderdeel1.MISO
  N4: Raspberry_Pi_1.GPIO11, Onderdeel1.MOSI
  N5: Raspberry_Pi_1.GPIO8, Onderdeel1.CE
